# Fritzing sketch DS18B20 (saved by Fritzing 0.9.2b)
breadboards: 1

parts:
  Bauteil1 = Arduino Uno (Rev3)
  DS1 = DS18B20 1-Wire Temperature Sensor [part_number=DS18B20]
  R1 = Resistor [tolerance=±5% resistance=4.7k package="0805 [SMD]"]

nets:
  N1: Bauteil1.D2, DS1.DQ, R1.Pin_0
  5V: Bauteil1.5V, DS1.VDD, R1.Pin_1
  GND: Bauteil1.GND, DS1.GND
