# Fritzing sketch GY-NEO6MV2-Raspberry-PI (saved by Fritzing 0.9.2b)

parts:
  GY-NEO6MV2 = SUP500F [package=sup500f]
  Raspberry_Pi1 = Raspberry Pi B+

nets:
  N1: GY-NEO6MV2.RX-I, Raspberry_Pi1.3v3
  N2: GY-NEO6MV2.TX-O, Raspberry_Pi1.GND
  N3: GY-NEO6MV2.GND, Raspberry_Pi1.GPIO14
  N4: GY-NEO6MV2.VCC, Raspberry_Pi1.GPIO15

notes:
  VCC: Red
  GND: Black
  RX: Yellow
  TX: Green
